# Fritzing sketch brute force microview connections (saved by Fritzing 0.9.3b)
breadboards: 1

parts:
  MV1 = MicroView [part_number=MicroView package="16pin wide"]
  R1 = Photocell (LDR) [package=THT]
  R2 = Resistor [tolerance=±5% resistance=330 package="2512 [SMD]"]
  R3 = Resistor [tolerance=±5% resistance=100k package="0603 [SMD]"]
  D2 = LTE-302 [package=lte-302]

nets:
  N1: MV1.A0, R1.pin_0, R3.Pin_1
  N2: MV1.GND, R3.Pin_0, D2.C
  N3: MV1.D3, R2.Pin_0
  N4: MV1.5V, R1.pin_1
  N5: R2.Pin_1, D2.A

custom parts:
  MicroView: MicroView - Chip-sized Arduino with OLED display.
